# Fritzing sketch schematic_Build_View (saved by Fritzing 0.9.3b)
breadboards: 1

parts:
  Part1 = Arduino Uno (Rev3) - ICSP
  hc-sr1 = hc-sr04
  LED2 = smd LED [color="Red (633nm)" package="0805 [SMD]"]
  LED3 = smd LED [color="Red (633nm)" package="0805 [SMD]"]
  LED4 = smd LED [color="Red (633nm)" package="0805 [SMD]"]
  LED1 = smd LED [color="Red (633nm)" package="0805 [SMD]"]
  R1 = Resistor [tolerance=±5% resistance=220 package="1206 [SMD]"]
  R2 = Resistor [tolerance=±5% resistance=220 package="1206 [SMD]"]
  L298N1 = IC, DIP package, 14 pins [chip_label=L298N]
  VCC1 = Battery block 9V
  M1 = DC Motor
  M2 = DC Motor

nets:
  5V: Part1.5V, hc-sr1.VCC
  N1: Part1.D8, L298N1.pin5
  N2: Part1.D9_PWM, L298N1.pin6
  N3: Part1.D10_PWM/SS, L298N1.pin7
  N4: Part1.D11_PWM/MOSI, L298N1.pin2
  N5: Part1.D12/MISO, LED3.anode
  N6: Part1.D13/SCK, LED1.anode
  N7: Part1.GND, R1.Pin_0, R2.Pin_0
  N8: Part1.D2, hc-sr1.Echo
  N9: Part1.D4, hc-sr1.Trig
  N10: Part1.D6_PWM, L298N1.pin3
  N11: Part1.D7, L298N1.pin4
  N12: hc-sr1.GND, L298N1.pin9, VCC1.+
  N13: LED2.cathode, R1.Pin_1
  N14: LED2.anode, LED1.cathode
  N15: LED3.cathode, LED4.anode
  N16: LED4.cathode, R2.Pin_1
  N17: L298N1.pin10, M2.pin_2
  N18: L298N1.pin11, M2.pin_1
  N19: L298N1.pin12, M1.pin_2
  N20: L298N1.pin13, M1.pin_1
  N21: L298N1.pin14, VCC1.-

custom parts:
  hc-sr04: This is a HC-SR04 Distance Sensor
