# Fritzing sketch schematic_Build_View (saved by Fritzing 0.9.3b)
breadboards: 1

parts:
  Part1 = Arduino Uno (Rev3) - ICSP
  hc-sr1 = hc-sr04
  LED2 = smd LED [color="Red (633nm)" package="0805 [SMD]"]
  LED3 = smd LED [color="Red (633nm)" package="0805 [SMD]"]
  LED4 = smd LED [color="Red (633nm)" package="0805 [SMD]"]
  LED1 = smd LED [color="Red (633nm)" package="0805 [SMD]"]
  R1 = Resistor [tolerance=±5% resistance=220 package="1206 [SMD]"]
  R2 = Resistor [tolerance=±5% resistance=220 package="1206 [SMD]"]

nets:
  5V: Part1.5V, hc-sr1.VCC
  N1: Part1.D8, LED3.anode
  N2: Part1.D9_PWM, hc-sr1.Trig
  N3: Part1.D10_PWM/SS, hc-sr1.Echo
  N4: Part1.D11_PWM/MOSI, LED1.anode
  GND: Part1.GND, hc-sr1.GND, R1.Pin_0, R2.Pin_0
  N5: LED2.cathode, R1.Pin_1
  N6: LED2.anode, LED1.cathode
  N7: LED3.cathode, LED4.anode
  N8: LED4.cathode, R2.Pin_1

custom parts:
  hc-sr04: This is a HC-SR04 Distance Sensor
